// Logisim project MUXdeMUX.circ as structural Verilog: 1 circuit, main circuit main
module main (
  input  D3,
  input  D2,
  input  D1,
  input  D0
);

  wire and_1_out, and_2_out, and_3_out, and_4_out, and_5_out, and_6_out, and_7_out, and_8_out, button_1_out,
       button_2_out, clock_1_out, not_1_out, not_2_out, not_3_out, not_4_out, not_5_out, not_6_out, or_1_out,
       t_ff_1_q, t_ff_1_qn, t_ff_2_q, t_ff_3_q, t_ff_3_qn, t_ff_4_q;

  Clock clock_1 (.out(clock_1_out));
  not not_1 (not_1_out, clock_1_out);
  Button button_1 (.out(button_1_out));
  T_Flip_Flop t_ff_1 (
    .clk(not_1_out), .T(1'b1), .Q(t_ff_1_q), .Qn(t_ff_1_qn), .reset(button_1_out));  // open: preset, en
  LED led_1 (.in(t_ff_1_q));
  LED led_2 (.in(t_ff_2_q));
  T_Flip_Flop t_ff_2 (.clk(t_ff_1_qn), .T(1'b1), .Q(t_ff_2_q), .reset(button_1_out));  // open: Qn, preset, en
  not not_2 (not_2_out, t_ff_1_q);
  not not_3 (not_3_out, t_ff_2_q);
  and and_1 (and_1_out, not_3_out, not_2_out, D0);
  and and_2 (and_2_out, not_3_out, t_ff_1_q, D1);
  and and_3 (and_3_out, not_2_out, t_ff_2_q, D2);
  and and_4 (and_4_out, t_ff_2_q, t_ff_1_q, D3);
  T_Flip_Flop t_ff_3 (
    .clk(not_4_out), .T(1'b1), .Q(t_ff_3_q), .Qn(t_ff_3_qn), .reset(button_2_out));  // open: preset, en
  not not_4 (not_4_out, clock_1_out);
  Button button_2 (.out(button_2_out));
  or or_1 (or_1_out, and_1_out, and_2_out, and_3_out, and_4_out);
  T_Flip_Flop t_ff_4 (.clk(t_ff_3_qn), .T(1'b1), .Q(t_ff_4_q), .reset(button_2_out));  // open: Qn, preset, en
  LED led_3 (.in(t_ff_3_q));
  LED led_4 (.in(t_ff_4_q));
  not not_5 (not_5_out, t_ff_3_q);
  not not_6 (not_6_out, t_ff_4_q);
  LED led_5 (.in(and_5_out));
  and and_5 (and_5_out, not_6_out, not_5_out, or_1_out);
  and and_6 (and_6_out, not_6_out, t_ff_3_q, or_1_out);
  and and_7 (and_7_out, not_5_out, t_ff_4_q, or_1_out);
  and and_8 (and_8_out, t_ff_4_q, t_ff_3_q, or_1_out);
  LED led_6 (.in(and_8_out));
  LED led_7 (.in(and_7_out));
  LED led_8 (.in(and_6_out));

  // Notes on the sheet:
  //   Takt
  //   Reset
  //   Reset
  //   Seriell (SER)
  //   A0
  //   A1
  //   A2
  //   A3
endmodule
