// Logisim project parDATA.circ as structural Verilog: 1 circuit, main circuit main
module main (
  input  Daten__seriell,
  input  Einlesen__E,
  input  \Binärdaten__D 
);

  wire and_1_out, clock_1_out, j_k_ff_1_q, j_k_ff_1_qn, nand_1_out, nand_2_out, not_1_out, not_2_out,
       not_3_out, not_4_out, not_5_out, or_1_out, s_r_ff_1_q, s_r_ff_1_qn;

  nand nand_1 (nand_1_out, Einlesen__E, \Binärdaten__D );
  Clock clock_1 (.out(clock_1_out));
  nand nand_2 (nand_2_out, Einlesen__E, not_1_out);
  not not_1 (not_1_out, \Binärdaten__D );
  not not_2 (not_2_out, clock_1_out);
  not not_3 (not_3_out, Daten__seriell);
  not not_4 (not_4_out, nand_1_out);
  not not_5 (not_5_out, nand_2_out);
  J_K_Flip_Flop j_k_ff_1 (
    .J(Daten__seriell), .clk(not_2_out), .K(not_3_out), .Q(j_k_ff_1_q), .Qn(j_k_ff_1_qn));  // open: preset, en, reset
  S_R_Flip_Flop s_r_ff_1 (
    .S(not_4_out), .clk(not_2_out), .R(not_5_out), .Q(s_r_ff_1_q), .Qn(s_r_ff_1_qn));  // open: preset, reset, en
  LED led_1 (.in(or_1_out));
  or or_1 (or_1_out, j_k_ff_1_q, s_r_ff_1_q);
  LED led_2 (.in(and_1_out));
  and and_1 (and_1_out, j_k_ff_1_qn, s_r_ff_1_qn);

  // Notes on the sheet:
  //   Takt (C)
endmodule
