// Logisim project parserparDATA.circ as structural Verilog: 1 circuit, main circuit main
module main (
  input  in_1,
  input  in_2,
  input  in_3,
  input  in_4,
  input  Seriell__S,
  input  Reset__R
);

  wire and_1_out, and_2_out, and_3_out, and_4_out, and_5_out, and_6_out, and_7_out, and_8_out, and_9_out,
       and_10_out, clock_1_out, d_ff_1_q, d_ff_2_q, d_ff_3_q, d_ff_4_q, j_k_ff_1_q, j_k_ff_2_q, j_k_ff_3_q,
       j_k_ff_3_qn, j_k_ff_4_q, j_k_ff_5_q, j_k_ff_5_qn, j_k_ff_6_q, j_k_ff_6_qn, j_k_ff_8_q, nand_1_out,
       not_1_out, not_2_out, not_3_out, not_4_out, not_5_out, not_6_out, not_7_out, not_8_out, not_9_out,
       not_10_out, not_11_out, not_12_out, not_13_out, or_1_out, or_2_out, or_3_out, or_4_out, t_ff_1_q,
       t_ff_1_qn, t_ff_2_q, t_ff_2_qn, t_ff_3_q, t_ff_3_qn, t_ff_4_q;

  Clock clock_1 (.out(clock_1_out));
  not not_1 (not_1_out, and_6_out);
  and and_1 (and_1_out, and_6_out, in_1);
  and and_2 (and_2_out, not_1_out, Seriell__S);
  T_Flip_Flop t_ff_1 (
    .clk(clock_1_out), .T(1'b1), .Q(t_ff_1_q), .Qn(t_ff_1_qn), .reset(and_5_out));  // open: preset, en
  or or_1 (or_1_out, and_1_out, and_2_out);
  not not_2 (not_2_out, or_1_out);
  not not_3 (not_3_out, clock_1_out);
  T_Flip_Flop t_ff_2 (.clk(t_ff_1_qn), .T(1'b1), .Q(t_ff_2_q), .Qn(t_ff_2_qn), .reset(and_5_out));  // open: preset, en
  not not_4 (not_4_out, and_6_out);
  J_K_Flip_Flop j_k_ff_1 (
    .J(or_1_out), .clk(not_3_out), .K(not_2_out), .Q(j_k_ff_1_q), .reset(Reset__R));  // open: Qn, preset, en
  LED led_1 (.in(j_k_ff_1_q));
  T_Flip_Flop t_ff_3 (.clk(t_ff_2_qn), .T(1'b1), .Q(t_ff_3_q), .Qn(t_ff_3_qn), .reset(and_5_out));  // open: preset, en
  and and_3 (and_3_out, and_6_out, in_2);
  and and_4 (and_4_out, not_4_out, j_k_ff_1_q);
  LED led_2 (.in(t_ff_1_q));
  LED led_3 (.in(t_ff_2_q));
  LED led_4 (.in(t_ff_3_q));
  T_Flip_Flop t_ff_4 (.clk(t_ff_3_qn), .T(1'b1), .Q(t_ff_4_q), .reset(and_5_out));  // open: Qn, preset, en
  LED led_5 (.in(t_ff_4_q));
  or or_2 (or_2_out, and_3_out, and_4_out);
  not not_5 (not_5_out, or_2_out);
  and and_5 (and_5_out, t_ff_1_q, t_ff_3_q);
  not not_6 (not_6_out, t_ff_1_q);
  and and_6 (and_6_out, not_6_out, t_ff_3_q);
  not not_7 (not_7_out, and_6_out);
  J_K_Flip_Flop j_k_ff_2 (
    .J(or_2_out), .clk(not_3_out), .K(not_5_out), .Q(j_k_ff_2_q), .reset(Reset__R));  // open: Qn, preset, en
  LED led_6 (.in(j_k_ff_2_q));
  not not_8 (not_8_out, and_6_out);
  and and_7 (and_7_out, and_6_out, in_3);
  and and_8 (and_8_out, not_7_out, j_k_ff_2_q);
  not not_9 (not_9_out, j_k_ff_1_q);
  not not_10 (not_10_out, nand_1_out);
  nand nand_1 (nand_1_out, not_8_out, clock_1_out);
  or or_3 (or_3_out, and_7_out, and_8_out);
  not not_11 (not_11_out, or_3_out);
  LED led_7 (.in(d_ff_1_q));
  D_Flip_Flop d_ff_1 (.clk(and_6_out), .D(j_k_ff_3_q), .Q(d_ff_1_q));  // open: Qn, preset, en, reset
  J_K_Flip_Flop j_k_ff_3 (
    .J(j_k_ff_1_q), .clk(not_10_out), .K(not_9_out), .Q(j_k_ff_3_q), .Qn(j_k_ff_3_qn));  // open: preset, en, reset
  not not_12 (not_12_out, and_6_out);
  J_K_Flip_Flop j_k_ff_4 (
    .J(or_3_out), .clk(not_3_out), .K(not_11_out), .Q(j_k_ff_4_q), .reset(Reset__R));  // open: Qn, preset, en
  LED led_8 (.in(j_k_ff_4_q));
  LED led_9 (.in(d_ff_2_q));
  D_Flip_Flop d_ff_2 (.clk(and_6_out), .D(j_k_ff_5_q), .Q(d_ff_2_q));  // open: Qn, preset, en, reset
  J_K_Flip_Flop j_k_ff_5 (
    .J(j_k_ff_3_q), .clk(not_10_out), .K(j_k_ff_3_qn), .Q(j_k_ff_5_q), .Qn(j_k_ff_5_qn));  // open: preset, en, reset
  and and_9 (and_9_out, and_6_out, in_4);
  or or_4 (or_4_out, and_9_out, and_10_out);
  and and_10 (and_10_out, not_12_out, j_k_ff_4_q);
  LED led_10 (.in(d_ff_3_q));
  D_Flip_Flop d_ff_3 (.clk(and_6_out), .D(j_k_ff_6_q), .Q(d_ff_3_q));  // open: Qn, preset, en, reset
  J_K_Flip_Flop j_k_ff_6 (
    .J(j_k_ff_5_q), .clk(not_10_out), .K(j_k_ff_5_qn), .Q(j_k_ff_6_q), .Qn(j_k_ff_6_qn));  // open: preset, en, reset
  J_K_Flip_Flop j_k_ff_7 (
    .J(or_4_out), .clk(not_3_out), .K(not_13_out), .Q(Seriell__S), .reset(Reset__R));  // open: Qn, preset, en
  not not_13 (not_13_out, or_4_out);
  LED led_11 (.in(d_ff_4_q));
  D_Flip_Flop d_ff_4 (.clk(and_6_out), .D(j_k_ff_8_q), .Q(d_ff_4_q));  // open: Qn, preset, en, reset
  J_K_Flip_Flop j_k_ff_8 (
    .J(j_k_ff_6_q), .clk(not_10_out), .K(j_k_ff_6_qn), .Q(j_k_ff_8_q));  // open: Qn, preset, en, reset
  LED led_12 (.in(Seriell__S));

  // Notes on the sheet:
  //   Takt (C)
  //   Einlesen (E)
  //   Binärdaten (D3)/8
  //   Binärdaten (D2)/4
  //   Q0
  //   A
  //   B
  //   C
  //   D
  //   Binärdaten (D1)/2
  //   Q1
  //   D
  //   Q2
  //   C
  //   Binärdaten (D0)/1
  //   B
  //   A
  //   Q3
endmodule
