// Logisim project parshiftregD.circ as structural Verilog: 1 circuit, main circuit main
module main (
  input  \Binärdaten__D0 ,
  input  \Binärdaten__D1 ,
  input  \Binärdaten__D2 ,
  input  \Binärdaten__D3 ,
  input  Einlesen__E,
  input  Seriell__S,
  input  Reset__R
);

  wire and_1_out, and_2_out, and_3_out, and_4_out, and_5_out, and_6_out, and_7_out, and_8_out, clock_1_out,
       j_k_ff_1_q, j_k_ff_2_q, j_k_ff_3_q, j_k_ff_4_q, not_1_out, not_2_out, not_3_out, not_4_out, not_5_out,
       not_6_out, not_7_out, not_8_out, not_9_out, or_1_out, or_2_out, or_3_out, or_4_out;

  not not_1 (not_1_out, Einlesen__E);
  and and_1 (and_1_out, Einlesen__E, \Binärdaten__D0 );
  and and_2 (and_2_out, not_1_out, Seriell__S);
  Clock clock_1 (.out(clock_1_out));
  or or_1 (or_1_out, and_1_out, and_2_out);
  not not_2 (not_2_out, or_1_out);
  not not_3 (not_3_out, clock_1_out);
  not not_4 (not_4_out, Einlesen__E);
  J_K_Flip_Flop j_k_ff_1 (
    .J(or_1_out), .clk(not_3_out), .K(not_2_out), .Q(j_k_ff_1_q), .reset(Reset__R));  // open: Qn, preset, en
  LED led_1 (.in(j_k_ff_1_q));
  and and_3 (and_3_out, Einlesen__E, \Binärdaten__D1 );
  and and_4 (and_4_out, not_4_out, j_k_ff_1_q);
  or or_2 (or_2_out, and_3_out, and_4_out);
  not not_5 (not_5_out, or_2_out);
  not not_6 (not_6_out, Einlesen__E);
  J_K_Flip_Flop j_k_ff_2 (
    .J(or_2_out), .clk(not_3_out), .K(not_5_out), .Q(j_k_ff_2_q), .reset(Reset__R));  // open: Qn, preset, en
  LED led_2 (.in(j_k_ff_2_q));
  and and_5 (and_5_out, Einlesen__E, \Binärdaten__D2 );
  or or_3 (or_3_out, and_5_out, and_6_out);
  and and_6 (and_6_out, not_6_out, j_k_ff_2_q);
  not not_7 (not_7_out, or_3_out);
  J_K_Flip_Flop j_k_ff_3 (
    .J(or_3_out), .clk(not_3_out), .K(not_7_out), .Q(j_k_ff_3_q), .reset(Reset__R));  // open: Qn, preset, en
  not not_8 (not_8_out, Einlesen__E);
  and and_7 (and_7_out, Einlesen__E, \Binärdaten__D3 );
  and and_8 (and_8_out, not_8_out, j_k_ff_3_q);
  LED led_3 (.in(j_k_ff_3_q));
  or or_4 (or_4_out, and_7_out, and_8_out);
  not not_9 (not_9_out, or_4_out);
  J_K_Flip_Flop j_k_ff_4 (
    .J(or_4_out), .clk(not_3_out), .K(not_9_out), .Q(j_k_ff_4_q), .reset(Reset__R));  // open: Qn, preset, en
  LED led_4 (.in(j_k_ff_4_q));

  // Notes on the sheet:
  //   Takt (C)
  //   Q0
  //   Q1
  //   Q2
  //   Q3
endmodule
