// Logisim project serDATA.circ as structural Verilog: 1 circuit, main circuit main
module main (
  input  in_1,
  input  in_2,
  input  d0,
  input  d1,
  input  d2,
  input  d3
);

  wire and_1_out, and_2_out, and_3_out, and_4_out, and_5_out, and_6_out, and_7_out, and_8_out, and_10_out,
       and_11_out, and_12_out, and_13_out, clock_1_out, not_1_out, not_2_out, not_3_out, not_4_out,
       not_5_out, not_6_out, or_1_out, s_r_ff_1_q, s_r_ff_1_qn, s_r_ff_2_q, s_r_ff_2_qn;

  Clock clock_1 (.out(clock_1_out));
  and and_1 (and_1_out, s_r_ff_1_qn, in_1);
  and and_2 (and_2_out, in_2, s_r_ff_1_q);
  S_R_Flip_Flop s_r_ff_1 (
    .S(and_1_out), .clk(clock_1_out), .R(and_2_out), .Q(s_r_ff_1_q), .Qn(s_r_ff_1_qn));  // open: preset, reset, en
  not not_1 (not_1_out, not_3_out);
  not not_2 (not_2_out, not_4_out);
  and and_3 (and_3_out, s_r_ff_2_qn, in_1);
  and and_4 (and_4_out, s_r_ff_1_qn, s_r_ff_2_q);
  and and_5 (and_5_out, not_2_out, not_1_out, d0);
  and and_6 (and_6_out, not_2_out, not_3_out, d1);
  and and_7 (and_7_out, not_1_out, not_4_out, d2);
  and and_8 (and_8_out, not_4_out, not_3_out, d3);
  not not_3 (not_3_out, s_r_ff_1_q);
  not not_4 (not_4_out, s_r_ff_2_q);
  S_R_Flip_Flop s_r_ff_2 (
    .S(and_3_out), .clk(s_r_ff_1_q), .R(and_4_out), .Q(s_r_ff_2_q), .Qn(s_r_ff_2_qn));  // open: preset, reset, en
  or or_1 (or_1_out, and_5_out, and_6_out, and_7_out, and_8_out);
  LED led_1 (.in(not_3_out));
  LED led_2 (.in(not_4_out));
  not not_5 (not_5_out, not_3_out);
  not not_6 (not_6_out, not_4_out);
  // AND_Gate and_9 has open pins: in3=not_5_out, in4=not_6_out, out=open
  // NOR_Gate nor_1 has open pins: in2=not_5_out, in3=not_6_out, out=open
  and and_10 (and_10_out, not_5_out, not_6_out, or_1_out);
  LED led_3 (.in(and_10_out));
  and and_11 (and_11_out, not_6_out, not_3_out, or_1_out);
  LED led_4 (.in(and_11_out));
  and and_12 (and_12_out, not_5_out, not_4_out, or_1_out);
  LED led_5 (.in(and_12_out));
  LED led_6 (.in(and_13_out));
  and and_13 (and_13_out, not_4_out, not_3_out, or_1_out);

  // Notes on the sheet:
  //   a0
  //   a1
  //   Y1
  //   y0
  //   y1
  //   y2
  //   y3
endmodule
