// Logisim project parshiftregJK.circ as structural Verilog: 1 circuit, main circuit main
module main (
  input  Einlesen__E,
  input  \Binärdaten__D0 ,
  input  \Binärdaten__D1 ,
  input  \Binärdaten__D2 ,
  input  \Binärdaten__D3 
);

  wire clock_1_out, j_k_ff_1_q, j_k_ff_1_qn, j_k_ff_2_q, j_k_ff_2_qn, j_k_ff_3_q, j_k_ff_3_qn, j_k_ff_4_q,
       j_k_ff_4_qn, nand_1_out, nand_2_out, nand_3_out, nand_4_out, nand_5_out, nand_6_out, nand_7_out,
       nand_8_out, not_1_out, not_2_out, not_3_out, not_4_out, not_5_out, not_6_out, not_7_out, not_8_out,
       not_9_out, not_10_out, not_11_out, not_12_out;

  Clock clock_1 (.out(clock_1_out));
  not not_1 (not_1_out, nand_1_out);
  nand nand_1 (nand_1_out, Einlesen__E, \Binärdaten__D0 );
  J_K_Flip_Flop j_k_ff_1 (
    .J(j_k_ff_4_q), .clk(clock_1_out), .K(j_k_ff_4_qn), .Q(j_k_ff_1_q), .Qn(j_k_ff_1_qn));  // open: preset, en, reset
  S_R_Flip_Flop s_r_ff_1 (.S(not_1_out), .R(not_2_out));  // open: clk, Q, Qn, preset, reset, en
  not not_2 (not_2_out, nand_2_out);
  nand nand_2 (nand_2_out, Einlesen__E, not_3_out);
  not not_3 (not_3_out, \Binärdaten__D0 );
  LED led_1 (.in(j_k_ff_1_q));
  not not_4 (not_4_out, nand_3_out);
  not not_5 (not_5_out, nand_4_out);
  nand nand_3 (nand_3_out, Einlesen__E, not_6_out);
  nand nand_4 (nand_4_out, Einlesen__E, \Binärdaten__D1 );
  not not_6 (not_6_out, \Binärdaten__D1 );
  LED led_2 (.in(j_k_ff_2_q));
  J_K_Flip_Flop j_k_ff_2 (
    .J(j_k_ff_1_q), .clk(clock_1_out), .K(j_k_ff_1_qn), .Q(j_k_ff_2_q), .Qn(j_k_ff_2_qn));  // open: preset, en, reset
  S_R_Flip_Flop s_r_ff_2 (.S(not_5_out), .R(not_4_out));  // open: clk, Q, Qn, preset, reset, en
  not not_7 (not_7_out, nand_5_out);
  nand nand_5 (nand_5_out, Einlesen__E, \Binärdaten__D2 );
  not not_8 (not_8_out, nand_6_out);
  nand nand_6 (nand_6_out, Einlesen__E, not_9_out);
  not not_9 (not_9_out, \Binärdaten__D2 );
  LED led_3 (.in(j_k_ff_3_q));
  J_K_Flip_Flop j_k_ff_3 (
    .J(j_k_ff_2_q), .clk(clock_1_out), .K(j_k_ff_2_qn), .Q(j_k_ff_3_q), .Qn(j_k_ff_3_qn));  // open: preset, en, reset
  S_R_Flip_Flop s_r_ff_3 (.S(not_7_out), .R(not_8_out));  // open: clk, Q, Qn, preset, reset, en
  not not_10 (not_10_out, nand_7_out);
  nand nand_7 (nand_7_out, Einlesen__E, \Binärdaten__D3 );
  LED led_4 (.in(j_k_ff_4_q));
  J_K_Flip_Flop j_k_ff_4 (
    .J(j_k_ff_3_q), .clk(clock_1_out), .K(j_k_ff_3_qn), .Q(j_k_ff_4_q), .Qn(j_k_ff_4_qn));  // open: preset, en, reset
  S_R_Flip_Flop s_r_ff_4 (.S(not_10_out), .R(not_11_out));  // open: clk, Q, Qn, preset, reset, en
  not not_11 (not_11_out, nand_8_out);
  nand nand_8 (nand_8_out, Einlesen__E, not_12_out);
  not not_12 (not_12_out, \Binärdaten__D3 );

  // Notes on the sheet:
  //   Takt (C)
  //   Q0
  //   Q1
  //   Q2
  //   Q3
endmodule
